// Logisim project Stage4.circ as structural Verilog: 3 circuits, main circuit main
module main (
);

  wire and_1_out, button_1_out, button_5_out, clock_1_out, j_k_ff_1_q, mod_6_synchronous_counter_1_r_tick,
       mod_9_synchronous_counter_1_r_tick, mod_9_synchronous_counter_2_r_tick;
  wire [3:0] mod_6_synchronous_counter_1_o_1, mod_9_synchronous_counter_1_o_1,
       mod_9_synchronous_counter_2_o_1, mod_9_synchronous_counter_3_o_1;

  Hex_Digit_Display hex_digit_display_1 ();  // open: value, dp
  Hex_Digit_Display hex_digit_display_2 ();  // open: value, dp
  Button button_1 (.out(button_1_out));
  Button button_2 ();  // open: out
  Hex_Digit_Display hex_digit_display_3 ();  // open: value, dp
  Hex_Digit_Display hex_digit_display_4 ();  // open: value, dp
  J_K_Flip_Flop j_k_ff_1 (.J(1'b1), .K(1'b1), .clk(button_1_out), .Q(j_k_ff_1_q));  // open: Qn, preset, reset
  Button button_3 ();  // open: out
  LED led_1 (.in(j_k_ff_1_q));
  Clock clock_1 (.out(clock_1_out));
  Button button_4 ();  // open: out
  Hex_Digit_Display hex_digit_display_5 ();  // open: value, dp
  Hex_Digit_Display hex_digit_display_6 ();  // open: value, dp
  and and_1 (and_1_out, j_k_ff_1_q, clock_1_out);
  LED led_2 ();  // open: in
  Hex_Digit_Display hex_digit_display_7 ();  // open: value, dp
  Button button_5 (.out(button_5_out));
  Hex_Digit_Display hex_digit_display_8 ();  // open: value, dp
  MOD_9_Synchronous_Counter mod_9_synchronous_counter_1 (
    .Reset(button_5_out), .Clock(and_1_out), .R_Tick(mod_9_synchronous_counter_1_r_tick),
    .O_1(mod_9_synchronous_counter_1_o_1[0]), .O_2(mod_9_synchronous_counter_1_o_1[1]),
    .O_3(mod_9_synchronous_counter_1_o_1[2]), .O_4(mod_9_synchronous_counter_1_o_1[3]));
  MOD_6_Synchronous_Counter mod_6_synchronous_counter_1 (
    .Reset(button_5_out), .Clock(mod_9_synchronous_counter_1_r_tick),
    .R_Tick(mod_6_synchronous_counter_1_r_tick), .O_1(mod_6_synchronous_counter_1_o_1[0]),
    .O_2(mod_6_synchronous_counter_1_o_1[1]), .O_3(mod_6_synchronous_counter_1_o_1[2]),
    .O_4(mod_6_synchronous_counter_1_o_1[3]));
  MOD_9_Synchronous_Counter mod_9_synchronous_counter_2 (
    .Reset(button_5_out), .Clock(mod_6_synchronous_counter_1_r_tick),
    .R_Tick(mod_9_synchronous_counter_2_r_tick), .O_1(mod_9_synchronous_counter_2_o_1[0]),
    .O_2(mod_9_synchronous_counter_2_o_1[1]), .O_3(mod_9_synchronous_counter_2_o_1[2]),
    .O_4(mod_9_synchronous_counter_2_o_1[3]));
  MOD_9_Synchronous_Counter mod_9_synchronous_counter_3 (
    .Reset(button_5_out), .Clock(mod_9_synchronous_counter_2_r_tick),
    .O_1(mod_9_synchronous_counter_3_o_1[0]), .O_2(mod_9_synchronous_counter_3_o_1[1]),
    .O_3(mod_9_synchronous_counter_3_o_1[2]), .O_4(mod_9_synchronous_counter_3_o_1[3]));  // open: R_Tick
  Hex_Digit_Display hex_digit_display_9 (.value(mod_9_synchronous_counter_3_o_1));  // open: dp
  Hex_Digit_Display hex_digit_display_10 (.value(mod_9_synchronous_counter_2_o_1));  // open: dp
  Hex_Digit_Display hex_digit_display_11 (.value(mod_9_synchronous_counter_1_o_1));  // open: dp
  Hex_Digit_Display hex_digit_display_12 (.value(mod_6_synchronous_counter_1_o_1));  // open: dp

  // Notes on the sheet:
  //   Elapsed Time
  //   Minutes
  //   :
  //   Start / Stop
  //   Start / Stop
  //   Seconds
  //   Stopwatch Interface
  //   Split
  //   Clock Started
  //   Reset
  //   Minutes
  //   Clock Started
  //   Split Time
  //   :
  //   Reset
  //   Seconds
  //   Minutes
  //   Elapsed Time
  //   :
  //   Seconds
endmodule

module MOD_9_Synchronous_Counter (
  input  Reset,
  input  Clock,
  output R_Tick,
  output O_1,
  output O_2,
  output O_3,
  output O_4
);

  wire and_1_out, and_2_out, or_1_out;

  or or_1 (or_1_out, R_Tick, Reset);
  J_K_Flip_Flop j_k_ff_1 (.J(1'b1), .K(1'b1), .clk(Clock), .Q(O_1), .reset(or_1_out));  // open: Qn, preset
  J_K_Flip_Flop j_k_ff_2 (.J(O_1), .K(O_1), .clk(Clock), .Q(O_2), .reset(or_1_out));  // open: Qn, preset
  and and_1 (and_1_out, O_1, O_2);
  J_K_Flip_Flop j_k_ff_3 (.J(and_1_out), .K(and_1_out), .clk(Clock), .Q(O_3), .reset(or_1_out));  // open: Qn, preset
  and and_2 (and_2_out, and_1_out, O_3);
  J_K_Flip_Flop j_k_ff_4 (.J(and_2_out), .K(and_2_out), .clk(Clock), .Q(O_4), .reset(or_1_out));  // open: Qn, preset
  and and_3 (R_Tick, O_2, O_4);
endmodule

module MOD_6_Synchronous_Counter (
  input  Reset,
  input  Clock,
  output R_Tick,
  output O_1,
  output O_2,
  output O_3,
  output O_4
);

  wire and_1_out, or_1_out;

  or or_1 (or_1_out, R_Tick, Reset);
  J_K_Flip_Flop j_k_ff_1 (.J(1'b1), .K(1'b1), .clk(Clock), .Q(O_1), .reset(or_1_out));  // open: Qn, preset
  J_K_Flip_Flop j_k_ff_2 (.J(O_1), .K(O_1), .clk(Clock), .Q(O_2), .reset(or_1_out));  // open: Qn, preset
  and and_1 (and_1_out, O_1, O_2);
  J_K_Flip_Flop j_k_ff_3 (.J(and_1_out), .K(and_1_out), .clk(Clock), .Q(O_3), .reset(or_1_out));  // open: Qn, preset
  and and_2 (R_Tick, O_2, O_3);

  assign O_4 = 1'b0;
endmodule
