// Logisim project Stage6.circ as structural Verilog: 6 circuits, main circuit main
module main (
);

  wire and_1_out, and_2_out, button_1_out, button_5_out, button_6_out, clock_1_out, j_k_ff_1_q,
       mod_6_synchronous_counter_1_r_tick, mod_9_synchronous_counter_1_r_tick,
       mod_9_synchronous_counter_2_r_tick;
  wire [3:0] mod_6_synchronous_counter_1_o_1, mod_9_synchronous_counter_1_o_1,
       mod_9_synchronous_counter_2_o_1, mod_9_synchronous_counter_3_o_1, multi_split_register_1_h_2_o_1,
       multi_split_register_1_m_1_o_1, multi_split_register_1_s_1_o_1, multi_split_register_1_s_2_o_1;

  Hex_Digit_Display hex_digit_display_1 ();  // open: value, dp
  Hex_Digit_Display hex_digit_display_2 ();  // open: value, dp
  Button button_1 (.out(button_1_out));
  Button button_2 ();  // open: out
  Hex_Digit_Display hex_digit_display_3 ();  // open: value, dp
  Hex_Digit_Display hex_digit_display_4 ();  // open: value, dp
  J_K_Flip_Flop j_k_ff_1 (.J(1'b1), .K(1'b1), .clk(button_1_out), .Q(j_k_ff_1_q));  // open: Qn, preset, reset
  Button button_3 ();  // open: out
  LED led_1 (.in(j_k_ff_1_q));
  Button button_4 ();  // open: out
  Hex_Digit_Display hex_digit_display_5 ();  // open: value, dp
  Hex_Digit_Display hex_digit_display_6 ();  // open: value, dp
  Clock clock_1 (.out(clock_1_out));
  LED led_2 ();  // open: in
  Hex_Digit_Display hex_digit_display_7 ();  // open: value, dp
  Button button_5 (.out(button_5_out));
  and and_1 (and_1_out, j_k_ff_1_q, clock_1_out);
  Hex_Digit_Display hex_digit_display_8 ();  // open: value, dp
  MOD_9_Synchronous_Counter mod_9_synchronous_counter_1 (
    .Reset(button_5_out), .Clock(and_1_out), .R_Tick(mod_9_synchronous_counter_1_r_tick),
    .O_1(mod_9_synchronous_counter_1_o_1[0]), .O_2(mod_9_synchronous_counter_1_o_1[1]),
    .O_3(mod_9_synchronous_counter_1_o_1[2]), .O_4(mod_9_synchronous_counter_1_o_1[3]));
  MOD_6_Synchronous_Counter mod_6_synchronous_counter_1 (
    .Reset(button_5_out), .Clock(mod_9_synchronous_counter_1_r_tick),
    .R_Tick(mod_6_synchronous_counter_1_r_tick), .O_1(mod_6_synchronous_counter_1_o_1[0]),
    .O_2(mod_6_synchronous_counter_1_o_1[1]), .O_3(mod_6_synchronous_counter_1_o_1[2]),
    .O_4(mod_6_synchronous_counter_1_o_1[3]));
  MOD_9_Synchronous_Counter mod_9_synchronous_counter_2 (
    .Reset(button_5_out), .Clock(mod_6_synchronous_counter_1_r_tick),
    .R_Tick(mod_9_synchronous_counter_2_r_tick), .O_1(mod_9_synchronous_counter_2_o_1[0]),
    .O_2(mod_9_synchronous_counter_2_o_1[1]), .O_3(mod_9_synchronous_counter_2_o_1[2]),
    .O_4(mod_9_synchronous_counter_2_o_1[3]));
  MOD_9_Synchronous_Counter mod_9_synchronous_counter_3 (
    .Reset(button_5_out), .Clock(mod_9_synchronous_counter_2_r_tick),
    .O_1(mod_9_synchronous_counter_3_o_1[0]), .O_2(mod_9_synchronous_counter_3_o_1[1]),
    .O_3(mod_9_synchronous_counter_3_o_1[2]), .O_4(mod_9_synchronous_counter_3_o_1[3]));  // open: R_Tick
  Hex_Digit_Display hex_digit_display_9 (.value(mod_9_synchronous_counter_3_o_1));  // open: dp
  Hex_Digit_Display hex_digit_display_10 (.value(mod_9_synchronous_counter_2_o_1));  // open: dp
  Hex_Digit_Display hex_digit_display_11 (.value(mod_9_synchronous_counter_1_o_1));  // open: dp
  Hex_Digit_Display hex_digit_display_12 (.value(mod_6_synchronous_counter_1_o_1));  // open: dp
  Button button_6 (.out(button_6_out));
  and and_2 (and_2_out, button_6_out, j_k_ff_1_q);
  Multi_Split_Register multi_split_register_1 (
    .Clock(and_2_out), .Reset(button_5_out), .S_1_I_1(mod_9_synchronous_counter_1_o_1[0]),
    .S_1_I_2(mod_9_synchronous_counter_1_o_1[1]), .S_1_I_3(mod_9_synchronous_counter_1_o_1[2]),
    .S_1_I_4(mod_9_synchronous_counter_1_o_1[3]), .S_2_I_1(mod_6_synchronous_counter_1_o_1[0]),
    .S_2_I_2(mod_6_synchronous_counter_1_o_1[1]), .S_2_I_3(mod_6_synchronous_counter_1_o_1[2]),
    .S_2_I_4(mod_6_synchronous_counter_1_o_1[3]), .M_1_I_1(mod_9_synchronous_counter_2_o_1[0]),
    .M_1_I_2(mod_9_synchronous_counter_2_o_1[1]), .M_1_I_3(mod_9_synchronous_counter_2_o_1[2]),
    .M_1_I_4(mod_9_synchronous_counter_2_o_1[3]), .M_2_O_1(mod_9_synchronous_counter_3_o_1[0]),
    .M_2_O_2(mod_9_synchronous_counter_3_o_1[1]), .M_2_O_3(mod_9_synchronous_counter_3_o_1[2]),
    .M_2_O_4(mod_9_synchronous_counter_3_o_1[3]), .S_1_O_1(multi_split_register_1_s_1_o_1[0]),
    .S_1_O_2(multi_split_register_1_s_1_o_1[1]), .S_1_O_3(multi_split_register_1_s_1_o_1[2]),
    .S_1_O_4(multi_split_register_1_s_1_o_1[3]), .S_2_O_1(multi_split_register_1_s_2_o_1[0]),
    .S_2_O_2(multi_split_register_1_s_2_o_1[1]), .S_2_O_3(multi_split_register_1_s_2_o_1[2]),
    .S_2_O_4(multi_split_register_1_s_2_o_1[3]), .M_1_O_1(multi_split_register_1_m_1_o_1[0]),
    .M_1_O_2(multi_split_register_1_m_1_o_1[1]), .M_1_O_3(multi_split_register_1_m_1_o_1[2]),
    .M_1_O_4(multi_split_register_1_m_1_o_1[3]), .H_2_O_1(multi_split_register_1_h_2_o_1[0]),
    .H_2_O_2(multi_split_register_1_h_2_o_1[1]), .H_2_O_3(multi_split_register_1_h_2_o_1[2]),
    .H_2_O_4(multi_split_register_1_h_2_o_1[3]));
  Hex_Digit_Display hex_digit_display_13 (.value(multi_split_register_1_h_2_o_1));  // open: dp
  Hex_Digit_Display hex_digit_display_14 (.value(multi_split_register_1_m_1_o_1));  // open: dp
  Hex_Digit_Display hex_digit_display_15 (.value(multi_split_register_1_s_2_o_1));  // open: dp
  Hex_Digit_Display hex_digit_display_16 (.value(multi_split_register_1_s_1_o_1));  // open: dp

  // Notes on the sheet:
  //   Elapsed Time
  //   Minutes
  //   :
  //   Start / Stop
  //   Start / Stop
  //   Seconds
  //   Stopwatch Interface
  //   Split
  //   Clock Started
  //   Reset
  //   Minutes
  //   Clock Started
  //   Split Time
  //   :
  //   Reset
  //   Seconds
  //   Minutes
  //   Elapsed Time
  //   :
  //   Seconds
  //   Split
  //   Minutes
  //   Split Time
  //   :
  //   Seconds
endmodule

module MOD_9_Synchronous_Counter (
  input  Reset,
  input  Clock,
  output R_Tick,
  output O_1,
  output O_2,
  output O_3,
  output O_4
);

  wire and_1_out, and_2_out, or_1_out;

  or or_1 (or_1_out, R_Tick, Reset);
  J_K_Flip_Flop j_k_ff_1 (.J(1'b1), .K(1'b1), .clk(Clock), .Q(O_1), .reset(or_1_out));  // open: Qn, preset
  J_K_Flip_Flop j_k_ff_2 (.J(O_1), .K(O_1), .clk(Clock), .Q(O_2), .reset(or_1_out));  // open: Qn, preset
  and and_1 (and_1_out, O_1, O_2);
  J_K_Flip_Flop j_k_ff_3 (.J(and_1_out), .K(and_1_out), .clk(Clock), .Q(O_3), .reset(or_1_out));  // open: Qn, preset
  and and_2 (and_2_out, and_1_out, O_3);
  J_K_Flip_Flop j_k_ff_4 (.J(and_2_out), .K(and_2_out), .clk(Clock), .Q(O_4), .reset(or_1_out));  // open: Qn, preset
  and and_3 (R_Tick, O_2, O_4);
endmodule

module MOD_6_Synchronous_Counter (
  input  Reset,
  input  Clock,
  output R_Tick,
  output O_1,
  output O_2,
  output O_3,
  output O_4
);

  wire and_1_out, or_1_out;

  or or_1 (or_1_out, R_Tick, Reset);
  J_K_Flip_Flop j_k_ff_1 (.J(1'b1), .K(1'b1), .clk(Clock), .Q(O_1), .reset(or_1_out));  // open: Qn, preset
  J_K_Flip_Flop j_k_ff_2 (.J(O_1), .K(O_1), .clk(Clock), .Q(O_2), .reset(or_1_out));  // open: Qn, preset
  and and_1 (and_1_out, O_1, O_2);
  J_K_Flip_Flop j_k_ff_3 (.J(and_1_out), .K(and_1_out), .clk(Clock), .Q(O_3), .reset(or_1_out));  // open: Qn, preset
  and and_2 (R_Tick, O_2, O_3);

  assign O_4 = 1'b0;
endmodule

module SixTeen_Bits_Register (
  input  Clock,
  input  Reset,
  input  S_1_I_1,
  input  S_1_I_2,
  input  S_1_I_3,
  input  S_1_I_4,
  input  S_2_I_1,
  input  S_2_I_2,
  input  S_2_I_3,
  input  S_2_I_4,
  input  M_1_I_1,
  input  M_1_I_2,
  input  M_1_I_3,
  input  M_1_I_4,
  input  M_2_I_1,
  input  M_2_I_2,
  input  M_2_I_3,
  input  M_2_I_4,
  output S_1_O_1,
  output S_1_O_2,
  output S_1_O_3,
  output S_1_O_4,
  output S_2_O_1,
  output S_2_O_2,
  output S_2_O_3,
  output S_2_O_4,
  output M_1_O_1,
  output M_1_O_2,
  output M_1_O_3,
  output M_1_O_4,
  output M_2_O_1,
  output M_2_O_2,
  output M_2_O_3,
  output M_2_O_4
);

  Four_Bits_Register four_bits_register_1 (
    .I_1(S_1_I_1), .I_2(S_1_I_2), .I_3(S_1_I_3), .I_4(S_1_I_4), .Clock(Clock), .Reset(Reset), .O_1(S_1_O_1),
    .O_2(S_1_O_2), .O_3(S_1_O_3), .O_4(S_1_O_4));
  Four_Bits_Register four_bits_register_2 (
    .I_1(S_2_I_1), .I_2(S_2_I_2), .I_3(S_2_I_3), .I_4(S_2_I_4), .Clock(Clock), .Reset(Reset), .O_1(S_2_O_1),
    .O_2(S_2_O_2), .O_3(S_2_O_3), .O_4(S_2_O_4));
  Four_Bits_Register four_bits_register_3 (
    .I_1(M_1_I_1), .I_2(M_1_I_2), .I_3(M_1_I_3), .I_4(M_1_I_4), .Clock(Clock), .Reset(Reset), .O_1(M_1_O_1),
    .O_2(M_1_O_2), .O_3(M_1_O_3), .O_4(M_1_O_4));
  Four_Bits_Register four_bits_register_4 (
    .I_1(M_2_I_1), .I_2(M_2_I_2), .I_3(M_2_I_3), .I_4(M_2_I_4), .Clock(Clock), .Reset(Reset), .O_1(M_2_O_1),
    .O_2(M_2_O_2), .O_3(M_2_O_3), .O_4(M_2_O_4));
  D_Flip_Flop d_ff_1 ();  // open: D, clk, Q, Qn, preset, reset
endmodule

module Four_Bits_Register (
  input  I_1,
  input  I_2,
  input  I_3,
  input  I_4,
  input  Clock,
  input  Reset,
  output O_1,
  output O_2,
  output O_3,
  output O_4
);

  D_Flip_Flop d_ff_1 (.D(I_1), .clk(Clock), .Q(O_1), .reset(Reset));  // open: Qn, preset
  D_Flip_Flop d_ff_2 (.D(I_2), .clk(Clock), .Q(O_2), .reset(Reset));  // open: Qn, preset
  D_Flip_Flop d_ff_3 (.D(I_3), .clk(Clock), .Q(O_3), .reset(Reset));  // open: Qn, preset
  D_Flip_Flop d_ff_4 (.D(I_4), .clk(Clock), .Q(O_4), .reset(Reset));  // open: Qn, preset
endmodule

module Multi_Split_Register (
  input  Clock,
  input  Reset,
  input  S_1_I_1,
  input  S_1_I_2,
  input  S_1_I_3,
  input  S_1_I_4,
  input  S_2_I_1,
  input  S_2_I_2,
  input  S_2_I_3,
  input  S_2_I_4,
  input  M_1_I_1,
  input  M_1_I_2,
  input  M_1_I_3,
  input  M_1_I_4,
  input  M_2_O_1,
  input  M_2_O_2,
  input  M_2_O_3,
  input  M_2_O_4,
  output S_1_O_1,
  output S_1_O_2,
  output S_1_O_3,
  output S_1_O_4,
  output S_2_O_1,
  output S_2_O_2,
  output S_2_O_3,
  output S_2_O_4,
  output M_1_O_1,
  output M_1_O_2,
  output M_1_O_3,
  output M_1_O_4,
  output H_2_O_1,
  output H_2_O_2,
  output H_2_O_3,
  output H_2_O_4
);

  wire [3:0] sixteen_bits_register_2_m_1_o_1, sixteen_bits_register_2_m_2_o_1,
       sixteen_bits_register_2_s_1_o_1, sixteen_bits_register_2_s_2_o_1, sixteen_bits_register_3_m_1_o_1,
       sixteen_bits_register_3_m_2_o_1, sixteen_bits_register_3_s_1_o_1, sixteen_bits_register_3_s_2_o_1,
       sixteen_bits_register_4_m_1_o_1, sixteen_bits_register_4_m_2_o_1, sixteen_bits_register_4_s_1_o_1,
       sixteen_bits_register_4_s_2_o_1, sixteen_bits_register_5_m_1_o_1, sixteen_bits_register_5_m_2_o_1,
       sixteen_bits_register_5_s_1_o_1, sixteen_bits_register_5_s_2_o_1;

  SixTeen_Bits_Register sixteen_bits_register_1 (
    .Clock(Clock), .Reset(Reset), .S_1_I_1(S_1_I_1), .S_1_I_2(S_1_I_2), .S_1_I_3(S_1_I_3), .S_1_I_4(S_1_I_4),
    .S_2_I_1(S_2_I_1), .S_2_I_2(S_2_I_2), .S_2_I_3(S_2_I_3), .S_2_I_4(S_2_I_4), .M_1_I_1(M_1_I_1),
    .M_1_I_2(M_1_I_2), .M_1_I_3(M_1_I_3), .M_1_I_4(M_1_I_4), .M_2_I_1(M_2_O_1), .M_2_I_2(M_2_O_2),
    .M_2_I_3(M_2_O_3), .M_2_I_4(M_2_O_4), .S_1_O_1(S_1_O_1), .S_1_O_2(S_1_O_2), .S_1_O_3(S_1_O_3),
    .S_1_O_4(S_1_O_4), .S_2_O_1(S_2_O_1), .S_2_O_2(S_2_O_2), .S_2_O_3(S_2_O_3), .S_2_O_4(S_2_O_4),
    .M_1_O_1(M_1_O_1), .M_1_O_2(M_1_O_2), .M_1_O_3(M_1_O_3), .M_1_O_4(M_1_O_4), .M_2_O_1(H_2_O_1),
    .M_2_O_2(H_2_O_2), .M_2_O_3(H_2_O_3), .M_2_O_4(H_2_O_4));
  Hex_Digit_Display hex_digit_display_1 (.value({H_2_O_4, H_2_O_3, H_2_O_2, H_2_O_1}));  // open: dp
  Hex_Digit_Display hex_digit_display_2 (.value({M_1_O_4, M_1_O_3, M_1_O_2, M_1_O_1}));  // open: dp
  Hex_Digit_Display hex_digit_display_3 (.value({S_2_O_4, S_2_O_3, S_2_O_2, S_2_O_1}));  // open: dp
  Hex_Digit_Display hex_digit_display_4 (.value({S_1_O_4, S_1_O_3, S_1_O_2, S_1_O_1}));  // open: dp
  Hex_Digit_Display hex_digit_display_5 (.value(sixteen_bits_register_2_m_2_o_1));  // open: dp
  SixTeen_Bits_Register sixteen_bits_register_2 (
    .Clock(Clock), .Reset(Reset), .S_1_I_1(S_1_O_1), .S_1_I_2(S_1_O_2), .S_1_I_3(S_1_O_3), .S_1_I_4(S_1_O_4),
    .S_2_I_1(S_2_O_1), .S_2_I_2(S_2_O_2), .S_2_I_3(S_2_O_3), .S_2_I_4(S_2_O_4), .M_1_I_1(M_1_O_1),
    .M_1_I_2(M_1_O_2), .M_1_I_3(M_1_O_3), .M_1_I_4(M_1_O_4), .M_2_I_1(H_2_O_1), .M_2_I_2(H_2_O_2),
    .M_2_I_3(H_2_O_3), .M_2_I_4(H_2_O_4), .S_1_O_1(sixteen_bits_register_2_s_1_o_1[0]),
    .S_1_O_2(sixteen_bits_register_2_s_1_o_1[1]), .S_1_O_3(sixteen_bits_register_2_s_1_o_1[2]),
    .S_1_O_4(sixteen_bits_register_2_s_1_o_1[3]), .S_2_O_1(sixteen_bits_register_2_s_2_o_1[0]),
    .S_2_O_2(sixteen_bits_register_2_s_2_o_1[1]), .S_2_O_3(sixteen_bits_register_2_s_2_o_1[2]),
    .S_2_O_4(sixteen_bits_register_2_s_2_o_1[3]), .M_1_O_1(sixteen_bits_register_2_m_1_o_1[0]),
    .M_1_O_2(sixteen_bits_register_2_m_1_o_1[1]), .M_1_O_3(sixteen_bits_register_2_m_1_o_1[2]),
    .M_1_O_4(sixteen_bits_register_2_m_1_o_1[3]), .M_2_O_1(sixteen_bits_register_2_m_2_o_1[0]),
    .M_2_O_2(sixteen_bits_register_2_m_2_o_1[1]), .M_2_O_3(sixteen_bits_register_2_m_2_o_1[2]),
    .M_2_O_4(sixteen_bits_register_2_m_2_o_1[3]));
  Hex_Digit_Display hex_digit_display_6 (.value(sixteen_bits_register_2_m_1_o_1));  // open: dp
  Hex_Digit_Display hex_digit_display_7 (.value(sixteen_bits_register_2_s_2_o_1));  // open: dp
  Hex_Digit_Display hex_digit_display_8 (.value(sixteen_bits_register_2_s_1_o_1));  // open: dp
  Hex_Digit_Display hex_digit_display_9 (.value(sixteen_bits_register_3_m_2_o_1));  // open: dp
  SixTeen_Bits_Register sixteen_bits_register_3 (
    .Clock(Clock), .Reset(Reset), .S_1_I_1(sixteen_bits_register_2_s_1_o_1[0]),
    .S_1_I_2(sixteen_bits_register_2_s_1_o_1[1]), .S_1_I_3(sixteen_bits_register_2_s_1_o_1[2]),
    .S_1_I_4(sixteen_bits_register_2_s_1_o_1[3]), .S_2_I_1(sixteen_bits_register_2_s_2_o_1[0]),
    .S_2_I_2(sixteen_bits_register_2_s_2_o_1[1]), .S_2_I_3(sixteen_bits_register_2_s_2_o_1[2]),
    .S_2_I_4(sixteen_bits_register_2_s_2_o_1[3]), .M_1_I_1(sixteen_bits_register_2_m_1_o_1[0]),
    .M_1_I_2(sixteen_bits_register_2_m_1_o_1[1]), .M_1_I_3(sixteen_bits_register_2_m_1_o_1[2]),
    .M_1_I_4(sixteen_bits_register_2_m_1_o_1[3]), .M_2_I_1(sixteen_bits_register_2_m_2_o_1[0]),
    .M_2_I_2(sixteen_bits_register_2_m_2_o_1[1]), .M_2_I_3(sixteen_bits_register_2_m_2_o_1[2]),
    .M_2_I_4(sixteen_bits_register_2_m_2_o_1[3]), .S_1_O_1(sixteen_bits_register_3_s_1_o_1[0]),
    .S_1_O_2(sixteen_bits_register_3_s_1_o_1[1]), .S_1_O_3(sixteen_bits_register_3_s_1_o_1[2]),
    .S_1_O_4(sixteen_bits_register_3_s_1_o_1[3]), .S_2_O_1(sixteen_bits_register_3_s_2_o_1[0]),
    .S_2_O_2(sixteen_bits_register_3_s_2_o_1[1]), .S_2_O_3(sixteen_bits_register_3_s_2_o_1[2]),
    .S_2_O_4(sixteen_bits_register_3_s_2_o_1[3]), .M_1_O_1(sixteen_bits_register_3_m_1_o_1[0]),
    .M_1_O_2(sixteen_bits_register_3_m_1_o_1[1]), .M_1_O_3(sixteen_bits_register_3_m_1_o_1[2]),
    .M_1_O_4(sixteen_bits_register_3_m_1_o_1[3]), .M_2_O_1(sixteen_bits_register_3_m_2_o_1[0]),
    .M_2_O_2(sixteen_bits_register_3_m_2_o_1[1]), .M_2_O_3(sixteen_bits_register_3_m_2_o_1[2]),
    .M_2_O_4(sixteen_bits_register_3_m_2_o_1[3]));
  Hex_Digit_Display hex_digit_display_10 (.value(sixteen_bits_register_3_m_1_o_1));  // open: dp
  Hex_Digit_Display hex_digit_display_11 (.value(sixteen_bits_register_3_s_2_o_1));  // open: dp
  Hex_Digit_Display hex_digit_display_12 (.value(sixteen_bits_register_3_s_1_o_1));  // open: dp
  SixTeen_Bits_Register sixteen_bits_register_4 (
    .Clock(Clock), .Reset(Reset), .S_1_I_1(sixteen_bits_register_3_s_1_o_1[0]),
    .S_1_I_2(sixteen_bits_register_3_s_1_o_1[1]), .S_1_I_3(sixteen_bits_register_3_s_1_o_1[2]),
    .S_1_I_4(sixteen_bits_register_3_s_1_o_1[3]), .S_2_I_1(sixteen_bits_register_3_s_2_o_1[0]),
    .S_2_I_2(sixteen_bits_register_3_s_2_o_1[1]), .S_2_I_3(sixteen_bits_register_3_s_2_o_1[2]),
    .S_2_I_4(sixteen_bits_register_3_s_2_o_1[3]), .M_1_I_1(sixteen_bits_register_3_m_1_o_1[0]),
    .M_1_I_2(sixteen_bits_register_3_m_1_o_1[1]), .M_1_I_3(sixteen_bits_register_3_m_1_o_1[2]),
    .M_1_I_4(sixteen_bits_register_3_m_1_o_1[3]), .M_2_I_1(sixteen_bits_register_3_m_2_o_1[0]),
    .M_2_I_2(sixteen_bits_register_3_m_2_o_1[1]), .M_2_I_3(sixteen_bits_register_3_m_2_o_1[2]),
    .M_2_I_4(sixteen_bits_register_3_m_2_o_1[3]), .S_1_O_1(sixteen_bits_register_4_s_1_o_1[0]),
    .S_1_O_2(sixteen_bits_register_4_s_1_o_1[1]), .S_1_O_3(sixteen_bits_register_4_s_1_o_1[2]),
    .S_1_O_4(sixteen_bits_register_4_s_1_o_1[3]), .S_2_O_1(sixteen_bits_register_4_s_2_o_1[0]),
    .S_2_O_2(sixteen_bits_register_4_s_2_o_1[1]), .S_2_O_3(sixteen_bits_register_4_s_2_o_1[2]),
    .S_2_O_4(sixteen_bits_register_4_s_2_o_1[3]), .M_1_O_1(sixteen_bits_register_4_m_1_o_1[0]),
    .M_1_O_2(sixteen_bits_register_4_m_1_o_1[1]), .M_1_O_3(sixteen_bits_register_4_m_1_o_1[2]),
    .M_1_O_4(sixteen_bits_register_4_m_1_o_1[3]), .M_2_O_1(sixteen_bits_register_4_m_2_o_1[0]),
    .M_2_O_2(sixteen_bits_register_4_m_2_o_1[1]), .M_2_O_3(sixteen_bits_register_4_m_2_o_1[2]),
    .M_2_O_4(sixteen_bits_register_4_m_2_o_1[3]));
  Hex_Digit_Display hex_digit_display_13 (.value(sixteen_bits_register_4_m_2_o_1));  // open: dp
  Hex_Digit_Display hex_digit_display_14 (.value(sixteen_bits_register_4_m_1_o_1));  // open: dp
  Hex_Digit_Display hex_digit_display_15 (.value(sixteen_bits_register_4_s_2_o_1));  // open: dp
  Hex_Digit_Display hex_digit_display_16 (.value(sixteen_bits_register_4_s_1_o_1));  // open: dp
  SixTeen_Bits_Register sixteen_bits_register_5 (
    .Clock(Clock), .Reset(Reset), .S_1_I_1(sixteen_bits_register_4_s_1_o_1[0]),
    .S_1_I_2(sixteen_bits_register_4_s_1_o_1[1]), .S_1_I_3(sixteen_bits_register_4_s_1_o_1[2]),
    .S_1_I_4(sixteen_bits_register_4_s_1_o_1[3]), .S_2_I_1(sixteen_bits_register_4_s_2_o_1[0]),
    .S_2_I_2(sixteen_bits_register_4_s_2_o_1[1]), .S_2_I_3(sixteen_bits_register_4_s_2_o_1[2]),
    .S_2_I_4(sixteen_bits_register_4_s_2_o_1[3]), .M_1_I_1(sixteen_bits_register_4_m_1_o_1[0]),
    .M_1_I_2(sixteen_bits_register_4_m_1_o_1[1]), .M_1_I_3(sixteen_bits_register_4_m_1_o_1[2]),
    .M_1_I_4(sixteen_bits_register_4_m_1_o_1[3]), .M_2_I_1(sixteen_bits_register_4_m_2_o_1[0]),
    .M_2_I_2(sixteen_bits_register_4_m_2_o_1[1]), .M_2_I_3(sixteen_bits_register_4_m_2_o_1[2]),
    .M_2_I_4(sixteen_bits_register_4_m_2_o_1[3]), .S_1_O_1(sixteen_bits_register_5_s_1_o_1[0]),
    .S_1_O_2(sixteen_bits_register_5_s_1_o_1[1]), .S_1_O_3(sixteen_bits_register_5_s_1_o_1[2]),
    .S_1_O_4(sixteen_bits_register_5_s_1_o_1[3]), .S_2_O_1(sixteen_bits_register_5_s_2_o_1[0]),
    .S_2_O_2(sixteen_bits_register_5_s_2_o_1[1]), .S_2_O_3(sixteen_bits_register_5_s_2_o_1[2]),
    .S_2_O_4(sixteen_bits_register_5_s_2_o_1[3]), .M_1_O_1(sixteen_bits_register_5_m_1_o_1[0]),
    .M_1_O_2(sixteen_bits_register_5_m_1_o_1[1]), .M_1_O_3(sixteen_bits_register_5_m_1_o_1[2]),
    .M_1_O_4(sixteen_bits_register_5_m_1_o_1[3]), .M_2_O_1(sixteen_bits_register_5_m_2_o_1[0]),
    .M_2_O_2(sixteen_bits_register_5_m_2_o_1[1]), .M_2_O_3(sixteen_bits_register_5_m_2_o_1[2]),
    .M_2_O_4(sixteen_bits_register_5_m_2_o_1[3]));
  Hex_Digit_Display hex_digit_display_17 (.value(sixteen_bits_register_5_m_2_o_1));  // open: dp
  Hex_Digit_Display hex_digit_display_18 (.value(sixteen_bits_register_5_m_1_o_1));  // open: dp
  Hex_Digit_Display hex_digit_display_19 (.value(sixteen_bits_register_5_s_2_o_1));  // open: dp
  Hex_Digit_Display hex_digit_display_20 (.value(sixteen_bits_register_5_s_1_o_1));  // open: dp

  // Notes on the sheet:
  //   Minutes
  //   Split Time 1
  //   Seconds
  //   :
  //   Split Time 2
  //   Minutes
  //   :
  //   Seconds
  //   Minutes
  //   Split Time 3
  //   :
  //   Seconds
  //   Minutes
  //   Split Time 4
  //   :
  //   Seconds
  //   Minutes
  //   Split Time 5
  //   :
  //   Seconds
endmodule
