// Logisim project Lab02.circ as structural Verilog: 3 circuits, main circuit main
module main (
  input  A,
  input  B,
  input  E,
  input  D,
  input  C_in,
  input  B1,
  input  A1,
  input  B2,
  input  A2,
  input  B3,
  input  A3,
  input  B4,
  input  A4,
  output Sum,
  output C_out,
  output Full_S,
  output Full_C_out,
  output out_18,
  output out_19,
  output out_20,
  output out_21,
  output out_22
);

  wire and_1_out, and_2_out, and_4_out, and_5_out, full_adder_1_c_out, full_adder_2_c_out,
       half_adder_1_c_out, not_1_out, not_2_out, xor_1_out, xor_2_out;

  not not_1 (not_1_out, A);
  xor xor_1 (xor_1_out, E, D);
  xor xor_2 (xor_2_out, E, D);
  not not_2 (not_2_out, B);
  xor xor_3 (Full_S, xor_1_out, C_in);
  Half_adder half_adder_1 (.A(A1), .B(B1), .Sum(out_18), .C_out(half_adder_1_c_out));
  and and_1 (and_1_out, not_1_out, B);
  and and_2 (and_2_out, not_2_out, A);
  and and_3 (C_out, B, A);
  and and_4 (and_4_out, xor_2_out, C_in);
  and and_5 (and_5_out, D, E);
  or or_1 (Sum, and_1_out, and_2_out);
  or or_2 (Full_C_out, and_4_out, and_5_out);
  Full_adder full_adder_1 (.A(A2), .B(B2), .C_in(half_adder_1_c_out), .Sum(out_19), .C_out(full_adder_1_c_out));
  Full_adder full_adder_2 (.A(A3), .B(B3), .C_in(full_adder_1_c_out), .Sum(out_20), .C_out(full_adder_2_c_out));
  Full_adder full_adder_3 (.A(A4), .B(B4), .C_in(full_adder_2_c_out), .Sum(out_21), .C_out(out_22));
endmodule

module Half_adder (
  input  A,
  input  B,
  output Sum,
  output C_out
);

  wire and_1_out, and_2_out, not_1_out, not_2_out;

  not not_1 (not_1_out, A);
  not not_2 (not_2_out, B);
  and and_1 (and_1_out, not_1_out, B);
  and and_2 (and_2_out, not_2_out, A);
  and and_3 (C_out, B, A);
  or or_1 (Sum, and_1_out, and_2_out);
endmodule

module Full_adder (
  input  A,
  input  B,
  input  C_in,
  output Sum,
  output C_out
);

  wire and_1_out, and_2_out, xor_1_out, xor_2_out;

  xor xor_1 (xor_1_out, A, B);
  xor xor_2 (xor_2_out, A, B);
  xor xor_3 (Sum, xor_1_out, C_in);
  and and_1 (and_1_out, xor_2_out, C_in);
  and and_2 (and_2_out, B, A);
  or or_1 (C_out, and_1_out, and_2_out);
endmodule
