// Logisim project Lab03.circ as structural Verilog: 1 circuit, main circuit main
module main (
  input  S,
  input  R,
  input  S_2,
  input  J,
  input  K,
  input  K_2,
  input  in_7,
  input  in_8,
  input  in_9,
  input  in_10,
  input  in_11,
  input  in_12,
  input  in_13,
  input  in_14
);

  wire and_1_out, and_2_out, clock_1_out, clock_2_out, clock_3_out, clock_4_out, clock_5_out, clock_6_out,
       clock_7_out, d_ff_1_q, d_ff_2_q, d_ff_3_q, d_ff_4_q, j_k_ff_1_q, j_k_ff_1_qn, j_k_ff_2_q, j_k_ff_2_qn,
       j_k_ff_3_q, j_k_ff_3_qn, nand_1_out, nand_2_out, nand_3_out, nand_4_out, nor_1_out, nor_2_out,
       nor_3_out, nor_4_out, not_1_out, not_2_out, t_ff_1_q, t_ff_1_qn;

  Clock clock_1 (.out(clock_1_out));
  Clock clock_2 (.out(clock_2_out));
  Clock clock_3 (.out(clock_3_out));
  Clock clock_4 (.out(clock_4_out));
  not not_1 (not_1_out, S_2);
  D_Flip_Flop d_ff_1 (.D(in_11), .clk(clock_4_out), .Q(d_ff_1_q));  // open: Qn, preset, reset
  nand nand_1 (nand_1_out, nand_4_out, J, clock_2_out);
  nand nand_2 (nand_2_out, clock_2_out, K, nand_3_out);
  Clock clock_5 (.out(clock_5_out));
  Clock clock_6 (.out(clock_6_out));
  J_K_Flip_Flop j_k_ff_1 (
    .J(in_10), .K(in_10), .clk(clock_3_out), .Q(j_k_ff_1_q), .Qn(j_k_ff_1_qn));  // open: preset, reset
  D_Flip_Flop d_ff_2 (.D(in_12), .clk(clock_4_out), .Q(d_ff_2_q));  // open: Qn, preset, reset
  LED led_1 (.in(d_ff_1_q));
  nor nor_1 (nor_1_out, S, nor_2_out);
  nor nor_2 (nor_2_out, nor_1_out, R);
  and and_1 (and_1_out, clock_1_out, not_1_out);
  and and_2 (and_2_out, clock_1_out, S_2);
  J_K_Flip_Flop j_k_ff_2 (
    .J(K_2), .K(in_7), .clk(clock_5_out), .Q(j_k_ff_2_q), .Qn(j_k_ff_2_qn));  // open: preset, reset
  T_Flip_Flop t_ff_1 (.T(in_8), .clk(clock_6_out), .Q(t_ff_1_q), .Qn(t_ff_1_qn));  // open: reset, preset
  not not_2 (not_2_out, in_9);
  Clock clock_7 (.out(clock_7_out));
  J_K_Flip_Flop j_k_ff_3 (
    .J(in_9), .K(not_2_out), .clk(clock_7_out), .Q(j_k_ff_3_q), .Qn(j_k_ff_3_qn));  // open: preset, reset
  LED led_2 (.in(j_k_ff_1_q));
  LED led_3 (.in(j_k_ff_1_qn));
  D_Flip_Flop d_ff_3 (.D(in_13), .clk(clock_4_out), .Q(d_ff_3_q));  // open: Qn, preset, reset
  LED led_4 (.in(d_ff_2_q));
  LED led_5 (.in(nor_1_out));
  LED led_6 (.in(nor_2_out));
  nand nand_3 (nand_3_out, nand_1_out, nand_4_out);
  nand nand_4 (nand_4_out, nand_3_out, nand_2_out);
  LED led_7 (.in(j_k_ff_2_q));
  LED led_8 (.in(j_k_ff_2_qn));
  LED led_9 (.in(d_ff_3_q));
  nor nor_3 (nor_3_out, and_1_out, nor_4_out);
  nor nor_4 (nor_4_out, nor_3_out, and_2_out);
  LED led_10 (.in(t_ff_1_q));
  LED led_11 (.in(t_ff_1_qn));
  LED led_12 (.in(j_k_ff_3_q));
  LED led_13 (.in(j_k_ff_3_qn));
  D_Flip_Flop d_ff_4 (.D(in_14), .clk(clock_4_out), .Q(d_ff_4_q));  // open: Qn, preset, reset
  LED led_14 (.in(d_ff_4_q));
  LED led_15 (.in(nand_3_out));
  LED led_16 (.in(nand_4_out));
  LED led_17 (.in(nor_3_out));
  LED led_18 (.in(nor_4_out));

  // Notes on the sheet:
  //   J
  //   Q
  //   Q'
  //   Q
  //   Q'
  //   Q
  //   Q'
  //   Q
  //   Q'
  //   Q
  //   Q'
  //   Q
  //   Q'
  //   Q
  //   Q'
endmodule
