// Logisim project lab04.circ as structural Verilog: 2 circuits, main circuit main
module main (
  input  in_1,
  input  in_2,
  input  in_3,
  input  in_4,
  input  in_5,
  input  in_6
);

  wire and_1_out, and_2_out, and_3_out, and_4_out, and_5_out, and_6_out, clock_1_out, clock_2_out,
       clock_3_out, clock_4_out, clock_5_out, j_k_ff_1_q, j_k_ff_2_q, j_k_ff_3_q, j_k_ff_4_q, j_k_ff_5_q,
       j_k_ff_6_q, j_k_ff_7_q, j_k_ff_8_q, j_k_ff_9_q, j_k_ff_10_q, j_k_ff_11_q, j_k_ff_12_q, j_k_ff_13_q,
       j_k_ff_14_q, j_k_ff_15_q;
  wire [2:0] d_ff_1_q;

  Clock clock_1 (.out(clock_1_out));
  Clock clock_2 (.out(clock_2_out));
  Clock clock_3 (.out(clock_3_out));
  Clock clock_4 (.out(clock_4_out));
  J_K_Flip_Flop #(.trigger("falling")) j_k_ff_1 (
    .J(in_1), .K(in_1), .clk(clock_1_out), .Q(j_k_ff_1_q), .reset(and_3_out));  // open: Qn, preset
  J_K_Flip_Flop j_k_ff_2 (.J(in_2), .K(in_2), .clk(clock_2_out), .Q(j_k_ff_2_q));  // open: Qn, preset, reset
  J_K_Flip_Flop j_k_ff_3 (.J(in_3), .K(in_3), .clk(clock_3_out), .Q(j_k_ff_3_q));  // open: Qn, preset, reset
  J_K_Flip_Flop j_k_ff_4 (
    .J(in_4), .K(in_4), .clk(clock_4_out), .Q(j_k_ff_4_q), .reset(and_5_out));  // open: Qn, preset
  LED led_1 (.in(j_k_ff_1_q));
  LED led_2 (.in(j_k_ff_2_q));
  LED led_3 (.in(j_k_ff_3_q));
  Clock clock_5 (.out(clock_5_out));
  J_K_Flip_Flop #(.trigger("falling")) j_k_ff_5 (
    .J(in_1), .K(in_1), .clk(j_k_ff_1_q), .Q(j_k_ff_5_q), .reset(and_3_out));  // open: Qn, preset
  J_K_Flip_Flop j_k_ff_6 (.J(in_2), .K(in_2), .clk(j_k_ff_2_q), .Q(j_k_ff_6_q));  // open: Qn, preset, reset
  J_K_Flip_Flop j_k_ff_7 (
    .J(j_k_ff_3_q), .K(j_k_ff_3_q), .clk(clock_3_out), .Q(j_k_ff_7_q));  // open: Qn, preset, reset
  J_K_Flip_Flop j_k_ff_8 (
    .J(j_k_ff_4_q), .K(j_k_ff_4_q), .clk(clock_4_out), .Q(j_k_ff_8_q), .reset(and_5_out));  // open: Qn, preset
  LED led_4 (.in(j_k_ff_4_q));
  LED led_5 (.in(j_k_ff_5_q));
  LED led_6 (.in(j_k_ff_6_q));
  LED led_7 (.in(j_k_ff_7_q));
  LED led_8 (.in(j_k_ff_8_q));
  D_Flip_Flop d_ff_1 (.D(j_k_ff_4_q), .clk(clock_4_out), .Q(d_ff_1_q[0]));  // open: Qn, preset, reset
  J_K_Flip_Flop j_k_ff_9 (
    .J(in_6), .K(in_6), .clk(clock_5_out), .Q(j_k_ff_9_q), .reset(and_6_out));  // open: Qn, preset
  J_K_Flip_Flop #(.trigger("falling")) j_k_ff_10 (
    .J(in_1), .K(in_1), .clk(j_k_ff_5_q), .Q(j_k_ff_10_q), .reset(and_3_out));  // open: Qn, preset
  J_K_Flip_Flop j_k_ff_11 (.J(in_2), .K(in_2), .clk(j_k_ff_6_q), .Q(j_k_ff_11_q));  // open: Qn, preset, reset
  and and_1 (and_1_out, j_k_ff_3_q, j_k_ff_7_q);
  and and_2 (and_2_out, j_k_ff_4_q, j_k_ff_8_q);
  LED led_9 (.in(d_ff_1_q[0]));
  LED led_10 (.in(j_k_ff_9_q));
  LED led_11 (.in(j_k_ff_10_q));
  LED led_12 (.in(j_k_ff_11_q));
  J_K_Flip_Flop j_k_ff_12 (
    .J(and_1_out), .K(and_1_out), .clk(clock_3_out), .Q(j_k_ff_12_q));  // open: Qn, preset, reset
  J_K_Flip_Flop j_k_ff_13 (
    .J(and_2_out), .K(and_2_out), .clk(clock_4_out), .Q(j_k_ff_13_q), .reset(and_5_out));  // open: Qn, preset
  D_Flip_Flop d_ff_2 (.D(j_k_ff_8_q), .clk(clock_4_out), .Q(d_ff_1_q[1]));  // open: Qn, preset, reset
  J_K_Flip_Flop j_k_ff_14 (
    .J(j_k_ff_9_q), .K(j_k_ff_9_q), .clk(clock_5_out), .Q(j_k_ff_14_q), .reset(and_6_out));  // open: Qn, preset
  and and_3 (and_3_out, j_k_ff_5_q, j_k_ff_10_q);
  LED led_13 (.in(j_k_ff_12_q));
  LED led_14 (.in(j_k_ff_13_q));
  LED led_15 (.in(d_ff_1_q[1]));
  LED led_16 (.in(j_k_ff_14_q));
  D_Flip_Flop d_ff_3 (.D(j_k_ff_13_q), .clk(clock_4_out), .Q(d_ff_1_q[2]));  // open: Qn, preset, reset
  and and_4 (and_4_out, j_k_ff_9_q, j_k_ff_14_q);
  J_K_Flip_Flop j_k_ff_15 (
    .J(and_4_out), .K(and_4_out), .clk(clock_5_out), .Q(j_k_ff_15_q), .reset(and_6_out));  // open: Qn, preset
  and and_5 (and_5_out, j_k_ff_8_q, j_k_ff_13_q);
  LED led_17 (.in(d_ff_1_q[2]));
  LED led_18 (.in(j_k_ff_15_q));
  and and_6 (and_6_out, j_k_ff_14_q, j_k_ff_15_q);
  Hex_Digit_Display hex_digit_display_1 (.value({in_5, d_ff_1_q}));  // open: dp
endmodule

module ShiftRegister (
  input  in_1,
  input  in_2,
  input  in_3,
  input  in_4,
  input  Serial_In,
  input  Clock_Countrol,
  input  in_7,
  input  in_8,
  input  in_9,
  input  in_10,
  input  S_in,
  input  C_control,
  input  in_13,
  input  in_14,
  input  in_15,
  input  in_16,
  input  Flow_Control,
  input  Serial_in_1,
  input  Serial_in_2,
  input  ClockControl
);

  wire and_1_out, and_2_out, and_3_out, and_4_out, and_5_out, and_6_out, and_7_out, and_8_out, and_9_out,
       and_10_out, and_11_out, clock_1_out, clock_2_out, clock_3_out, d_ff_1_q, d_ff_2_q, d_ff_3_q, d_ff_4_q,
       d_ff_5_q, d_ff_6_q, d_ff_7_q, d_ff_8_q, d_ff_9_q, d_ff_10_q, d_ff_11_q, d_ff_12_q, not_1_out,
       or_1_out, or_2_out, or_3_out, or_4_out, or_5_out, or_6_out, or_7_out, or_8_out, or_9_out, or_10_out,
       or_11_out, or_12_out, or_13_out, or_14_out, or_15_out, or_16_out, or_17_out, or_18_out;

  Clock clock_1 (.out(clock_1_out));
  not not_1 (not_1_out, Flow_Control);
  and and_1 (and_1_out, ClockControl, clock_1_out);
  LED S_out (.in(d_ff_2_q));
  LED led_1 (.in(d_ff_3_q));
  Clock clock_2 (.out(clock_2_out));
  Clock clock_3 (.out(clock_3_out));
  and and_2 (and_2_out, Clock_Countrol, clock_2_out);
  and and_3 (and_3_out, C_control, clock_3_out);
  or or_1 (or_1_out, Serial_in_1, Serial_in_2);
  or or_2 (or_2_out, in_13, or_5_out);
  or or_3 (or_3_out, Serial_In, in_1);
  D_Flip_Flop d_ff_1 (.D(or_3_out), .clk(and_2_out), .Q(d_ff_1_q));  // open: Qn, preset, reset
  or or_4 (or_4_out, in_7, d_ff_5_q);
  D_Flip_Flop d_ff_2 (.D(or_4_out), .clk(and_3_out), .Q(d_ff_2_q));  // open: Qn, preset, reset
  and and_4 (and_4_out, not_1_out, or_1_out);
  LED led_2 (.in(d_ff_1_q));
  and and_5 (and_5_out, Flow_Control, d_ff_8_q);
  or or_5 (or_5_out, and_4_out, and_5_out);
  D_Flip_Flop d_ff_3 (.D(or_2_out), .clk(and_1_out), .Q(d_ff_3_q));  // open: Qn, preset, reset
  or or_6 (or_6_out, d_ff_1_q, in_2);
  D_Flip_Flop d_ff_4 (.D(or_6_out), .clk(and_2_out), .Q(d_ff_4_q));  // open: Qn, preset, reset
  or or_7 (or_7_out, in_8, d_ff_7_q);
  D_Flip_Flop d_ff_5 (.D(or_7_out), .clk(and_3_out), .Q(d_ff_5_q));  // open: Qn, preset, reset
  LED led_3 (.in(d_ff_4_q));
  LED led_4 (.in(d_ff_5_q));
  or or_8 (or_8_out, in_14, or_11_out);
  or or_9 (or_9_out, d_ff_4_q, in_3);
  D_Flip_Flop d_ff_6 (.D(or_9_out), .clk(and_2_out), .Q(d_ff_6_q));  // open: Qn, preset, reset
  or or_10 (or_10_out, in_9, d_ff_10_q);
  and and_6 (and_6_out, d_ff_3_q, not_1_out);
  or or_11 (or_11_out, and_6_out, and_7_out);
  LED led_5 (.in(d_ff_6_q));
  D_Flip_Flop d_ff_7 (.D(or_10_out), .clk(and_3_out), .Q(d_ff_7_q));  // open: Qn, preset, reset
  and and_7 (and_7_out, Flow_Control, d_ff_11_q);
  D_Flip_Flop d_ff_8 (.D(or_8_out), .clk(and_1_out), .Q(d_ff_8_q));  // open: Qn, preset, reset
  or or_12 (or_12_out, d_ff_6_q, in_4);
  D_Flip_Flop d_ff_9 (.D(or_12_out), .clk(and_2_out), .Q(d_ff_9_q));  // open: Qn, preset, reset
  LED led_6 (.in(d_ff_7_q));
  LED led_7 (.in(d_ff_8_q));
  or or_13 (or_13_out, in_10, S_in);
  D_Flip_Flop d_ff_10 (.D(or_13_out), .clk(and_3_out), .Q(d_ff_10_q));  // open: Qn, preset, reset
  LED led_8 (.in(d_ff_10_q));
  or or_14 (or_14_out, in_15, or_15_out);
  LED Serial_Out (.in(d_ff_9_q));
  and and_8 (and_8_out, d_ff_8_q, not_1_out);
  or or_15 (or_15_out, and_8_out, and_9_out);
  and and_9 (and_9_out, Flow_Control, d_ff_12_q);
  D_Flip_Flop d_ff_11 (.D(or_14_out), .clk(and_1_out), .Q(d_ff_11_q));  // open: Qn, preset, reset
  LED led_9 (.in(d_ff_11_q));
  or or_16 (or_16_out, in_16, or_17_out);
  and and_10 (and_10_out, d_ff_11_q, not_1_out);
  and and_11 (and_11_out, Flow_Control, or_18_out);
  or or_17 (or_17_out, and_10_out, and_11_out);
  D_Flip_Flop d_ff_12 (.D(or_16_out), .clk(and_1_out), .Q(d_ff_12_q));  // open: Qn, preset, reset
  LED led_10 (.in(d_ff_12_q));
  or or_18 (or_18_out, Serial_in_1, Serial_in_2);
endmodule
