// Logisim project Lab05.circ as structural Verilog: 1 circuit, main circuit main
module main (
  input  in_1,
  input  in_2,
  input  in_3,
  input  in_4,
  input  in_5,
  input  in_6,
  input  in_7,
  input  in_8,
  input  in_9,
  input  in_10,
  input  in_11,
  input  in_12,
  input  in_13,
  input  in_14,
  input  in_15,
  input  in_16,
  input  in_17,
  input  in_18,
  input  in_19,
  input  in_20,
  input  in_21,
  input  in_22,
  input  in_23,
  input  in_24,
  input  in_25
);

  wire and_1_out, and_2_out, and_3_out, and_4_out, and_5_out, and_6_out, and_7_out, and_8_out, and_9_out,
       and_10_out, and_11_out, and_12_out, and_13_out, and_14_out, and_15_out, and_16_out, and_17_out,
       and_18_out, and_19_out, and_20_out, and_21_out, and_22_out, clock_1_out, clock_2_out, clock_3_out,
       clock_4_out, clock_5_out, clock_6_out, clock_7_out, d_ff_1_q, d_ff_2_q, d_ff_3_q, d_ff_5_q, d_ff_6_q,
       d_ff_7_q, d_ff_8_q, d_ff_9_q, d_ff_10_q, d_ff_11_q, d_ff_12_q, d_ff_13_q, d_ff_14_q, d_ff_15_q,
       d_ff_16_q, d_ff_17_q, d_ff_18_q, d_ff_19_q, d_ff_20_q, d_ff_21_q, d_ff_22_q, d_ff_23_q, d_ff_24_q,
       d_ff_25_q, d_ff_26_q, d_ff_27_q, Left_out, not_1_out, not_2_out, not_3_out, not_4_out, not_5_out,
       not_6_out, or_1_out, or_2_out, or_3_out, or_4_out, or_5_out, or_6_out, or_7_out, or_8_out, or_9_out,
       or_10_out, or_11_out, or_12_out, or_13_out, Right_out;

  not not_1 (not_1_out, in_17);
  Clock clock_1 (.out(clock_1_out));
  Clock clock_2 (.out(clock_2_out));
  Clock clock_3 (.out(clock_3_out));
  not not_2 (not_2_out, in_11);
  not not_3 (not_3_out, in_20);
  and and_1 (and_1_out, in_20, in_22);
  not not_4 (not_4_out, in_8);
  not not_5 (not_5_out, in_14);
  Clock clock_4 (.out(clock_4_out));
  and and_2 (and_2_out, in_17, in_18);
  and and_3 (and_3_out, in_18, not_1_out);
  or or_1 (or_1_out, and_3_out, d_ff_10_q);
  D_Flip_Flop d_ff_1 (.D(or_1_out), .clk(clock_5_out), .Q(d_ff_1_q), .reset(in_19));  // open: Qn, preset
  Clock clock_5 (.out(clock_5_out));
  and and_4 (and_4_out, not_3_out, d_ff_11_q);
  or or_2 (or_2_out, and_1_out, and_4_out);
  D_Flip_Flop d_ff_2 (.D(or_2_out), .clk(and_5_out), .Q(d_ff_2_q), .reset(in_23));  // open: Qn, preset
  and and_5 (and_5_out, clock_1_out, in_24);
  and and_6 (and_6_out, clock_1_out, in_25);
  D_Flip_Flop d_ff_3 (.D(in_1), .clk(clock_2_out), .Q(d_ff_3_q), .reset(in_2));  // open: Qn, preset
  not not_6 (not_6_out, in_5);
  D_Flip_Flop d_ff_4 (.D(d_ff_7_q), .clk(clock_3_out), .reset(in_6));  // open: Q, Qn, preset
  and Right (Right_out, in_8, in_9);
  and Left (Left_out, in_9, not_4_out);
  Clock clock_6 (.out(clock_6_out));
  and and_7 (and_7_out, in_11, in_12);
  and and_8 (and_8_out, in_12, not_2_out);
  D_Flip_Flop d_ff_5 (.D(or_3_out), .clk(clock_7_out), .Q(d_ff_5_q), .reset(in_13));  // open: Qn, preset
  Clock clock_7 (.out(clock_7_out));
  and and_9 (and_9_out, in_14, in_15);
  and and_10 (and_10_out, in_15, not_5_out);
  LED led_1 (.in(d_ff_1_q));
  D_Flip_Flop d_ff_6 (.D(d_ff_3_q), .clk(clock_2_out), .Q(d_ff_6_q), .reset(in_2));  // open: Qn, preset
  LED led_2 (.in(d_ff_3_q));
  and and_11 (and_11_out, in_4, not_6_out);
  and and_12 (and_12_out, in_5, in_3);
  D_Flip_Flop d_ff_7 (.D(d_ff_16_q), .clk(clock_3_out), .Q(d_ff_7_q), .reset(in_6));  // open: Qn, preset
  D_Flip_Flop d_ff_8 (.D(Left_out), .clk(clock_6_out), .Q(d_ff_8_q), .reset(in_10));  // open: Qn, preset
  or or_3 (or_3_out, and_8_out, d_ff_14_q);
  LED led_3 (.in(d_ff_5_q));
  or or_4 (or_4_out, and_10_out, and_17_out);
  D_Flip_Flop d_ff_9 (.D(or_4_out), .clk(clock_4_out), .Q(d_ff_9_q), .reset(in_16));  // open: Qn, preset
  or or_5 (or_5_out, d_ff_1_q, d_ff_18_q);
  D_Flip_Flop d_ff_10 (.D(or_5_out), .clk(clock_5_out), .Q(d_ff_10_q), .reset(in_19));  // open: Qn, preset
  and and_13 (and_13_out, in_20, d_ff_2_q);
  and and_14 (and_14_out, not_3_out, d_ff_20_q);
  or or_6 (or_6_out, and_13_out, and_14_out);
  D_Flip_Flop d_ff_11 (.D(or_6_out), .clk(and_5_out), .Q(d_ff_11_q), .reset(in_23));  // open: Qn, preset
  D_Flip_Flop d_ff_12 (.D(d_ff_2_q), .clk(and_6_out), .Q(d_ff_12_q), .reset(in_23));  // open: Qn, preset
  D_Flip_Flop d_ff_13 (.D(Right_out), .clk(clock_6_out), .Q(d_ff_13_q), .reset(in_10));  // open: Qn, preset
  LED led_4 (.in(d_ff_8_q));
  or or_7 (or_7_out, d_ff_5_q, and_7_out);
  D_Flip_Flop d_ff_14 (.D(or_7_out), .clk(clock_7_out), .Q(d_ff_14_q), .reset(in_13));  // open: Qn, preset
  LED led_5 (.in(d_ff_9_q));
  LED led_6 (.in(d_ff_10_q));
  LED led_7 (.in(d_ff_12_q));
  D_Flip_Flop d_ff_15 (.D(d_ff_6_q), .clk(clock_2_out), .Q(d_ff_15_q), .reset(in_2));  // open: Qn, preset
  LED led_8 (.in(d_ff_6_q));
  or or_8 (or_8_out, and_11_out, and_12_out);
  D_Flip_Flop d_ff_16 (.D(d_ff_22_q), .clk(clock_3_out), .Q(d_ff_16_q), .reset(in_6));  // open: Qn, preset
  LED led_9 (.in(d_ff_14_q));
  or or_9 (or_9_out, and_9_out, and_18_out);
  D_Flip_Flop d_ff_17 (.D(or_9_out), .clk(clock_4_out), .Q(d_ff_17_q), .reset(in_16));  // open: Qn, preset
  or or_10 (or_10_out, d_ff_10_q, and_2_out);
  D_Flip_Flop d_ff_18 (.D(or_10_out), .clk(clock_5_out), .Q(d_ff_18_q), .reset(in_19));  // open: Qn, preset
  and and_15 (and_15_out, in_20, d_ff_11_q);
  D_Flip_Flop d_ff_19 (.D(d_ff_11_q), .clk(and_6_out), .Q(d_ff_19_q), .reset(in_23));  // open: Qn, preset
  LED led_10 (.in(d_ff_15_q));
  LED led_11 (.in(or_8_out));
  LED led_12 (.in(d_ff_13_q));
  LED led_13 (.in(d_ff_18_q));
  and and_16 (and_16_out, not_3_out, d_ff_23_q);
  or or_11 (or_11_out, and_15_out, and_16_out);
  D_Flip_Flop d_ff_20 (.D(or_11_out), .clk(and_5_out), .Q(d_ff_20_q), .reset(in_23));  // open: Qn, preset
  LED led_14 (.in(d_ff_19_q));
  D_Flip_Flop d_ff_21 (.D(d_ff_15_q), .clk(clock_2_out), .Q(d_ff_21_q), .reset(in_2));  // open: Qn, preset
  D_Flip_Flop d_ff_22 (.D(in_7), .clk(clock_3_out), .Q(d_ff_22_q), .reset(in_6));  // open: Qn, preset
  and and_17 (and_17_out, in_14, d_ff_17_q);
  and and_18 (and_18_out, d_ff_9_q, not_5_out);
  LED led_15 (.in(d_ff_17_q));
  and and_19 (and_19_out, in_20, d_ff_20_q);
  or or_12 (or_12_out, and_19_out, and_20_out);
  D_Flip_Flop d_ff_23 (.D(or_12_out), .clk(and_5_out), .Q(d_ff_23_q), .reset(in_23));  // open: Qn, preset
  D_Flip_Flop d_ff_24 (.D(d_ff_20_q), .clk(and_6_out), .Q(d_ff_24_q), .reset(in_23));  // open: Qn, preset
  LED led_16 (.in(d_ff_21_q));
  and and_20 (and_20_out, not_3_out, d_ff_26_q);
  LED led_17 (.in(d_ff_24_q));
  and and_21 (and_21_out, in_20, d_ff_23_q);
  D_Flip_Flop d_ff_25 (.D(d_ff_23_q), .clk(and_6_out), .Q(d_ff_25_q), .reset(in_23));  // open: Qn, preset
  and and_22 (and_22_out, not_3_out, in_21);
  or or_13 (or_13_out, and_21_out, and_22_out);
  D_Flip_Flop d_ff_26 (.D(or_13_out), .clk(and_5_out), .Q(d_ff_26_q), .reset(in_23));  // open: Qn, preset
  LED led_18 (.in(d_ff_25_q));
  D_Flip_Flop d_ff_27 (.D(d_ff_26_q), .clk(and_6_out), .Q(d_ff_27_q), .reset(in_23));  // open: Qn, preset
  LED led_19 (.in(d_ff_27_q));
endmodule
