// Logisim project Alarm_Clock.circ as structural Verilog: 8 circuits, main circuit Main_clock
module Main_clock (
  input  Start,
  input  Set_Time,
  input  M_plus,
  input  H_plus,
  input  Set_Alarm,
  input  Enable_Alarm_LED
);

  wire alarm_sub_clock_1_out_a_h_1, alarm_sub_clock_1_out_a_h_2, alarm_sub_clock_1_out_a_h_3,
       alarm_sub_clock_1_out_a_h_4, alarm_sub_clock_1_out_a_h_5, alarm_sub_clock_1_out_a_h_6,
       alarm_sub_clock_1_out_a_m_6_1, alarm_sub_clock_1_out_a_m_6_2, alarm_sub_clock_1_out_a_m_6_3,
       alarm_sub_clock_1_out_a_m_9_1, alarm_sub_clock_1_out_a_m_9_2, alarm_sub_clock_1_out_a_m_9_3,
       alarm_sub_clock_1_out_a_m_9_4, and_1_out, and_2_out, enable_alarm_1_out_alarm_led,
       enable_alarm_1_out_h_6, minutes_and_hours_1_out_clock, minutes_and_hours_1_out_h_1,
       minutes_and_hours_1_out_h_2, minutes_and_hours_1_out_h_3, minutes_and_hours_1_out_h_4,
       minutes_and_hours_1_out_h_5, minutes_and_hours_1_out_h_6, minutes_and_hours_1_out_m_6_1,
       minutes_and_hours_1_out_m_6_2, minutes_and_hours_1_out_m_6_3, minutes_and_hours_1_out_m_9_1,
       minutes_and_hours_1_out_m_9_2, minutes_and_hours_1_out_m_9_3, minutes_and_hours_1_out_m_9_4,
       not_1_out, or_1_out;
  wire [0:0] enable_alarm_1_out_h_5;
  wire [2:0] enable_alarm_1_out_m_6_1;
  wire [3:0] enable_alarm_1_out_h_1, enable_alarm_1_out_m_9_1;

  not not_1 (not_1_out, Set_Alarm);
  or or_1 (or_1_out, Set_Time, Set_Alarm);
  and and_1 (and_1_out, not_1_out, M_plus);
  and and_2 (and_2_out, not_1_out, H_plus);
  Minutes_and_Hours minutes_and_hours_1 (
    .Out_Clock(minutes_and_hours_1_out_clock), .Out_H_1(minutes_and_hours_1_out_h_1),
    .Out_H_2(minutes_and_hours_1_out_h_2), .Out_H_3(minutes_and_hours_1_out_h_3),
    .Out_H_4(minutes_and_hours_1_out_h_4), .Out_H_5(minutes_and_hours_1_out_h_5),
    .Out_H_6(minutes_and_hours_1_out_h_6), .Out_M_6_1(minutes_and_hours_1_out_m_6_1),
    .Out_M_6_2(minutes_and_hours_1_out_m_6_2), .Out_M_6_3(minutes_and_hours_1_out_m_6_3),
    .Out_M_9_1(minutes_and_hours_1_out_m_9_1), .Out_M_9_2(minutes_and_hours_1_out_m_9_2),
    .Out_M_9_3(minutes_and_hours_1_out_m_9_3), .Out_M_9_4(minutes_and_hours_1_out_m_9_4), .Clock(Start),
    .Set_Time(or_1_out), .M_plus(and_1_out), .H_plus(and_2_out));
  Alarm_sub_Clock alarm_sub_clock_1 (
    .Out_A_H_1(alarm_sub_clock_1_out_a_h_1), .Out_A_H_2(alarm_sub_clock_1_out_a_h_2),
    .Out_A_H_3(alarm_sub_clock_1_out_a_h_3), .Out_A_H_4(alarm_sub_clock_1_out_a_h_4),
    .Out_A_H_5(alarm_sub_clock_1_out_a_h_5), .Out_A_H_6(alarm_sub_clock_1_out_a_h_6),
    .Out_A_M_6_1(alarm_sub_clock_1_out_a_m_6_1), .Out_A_M_6_2(alarm_sub_clock_1_out_a_m_6_2),
    .Out_A_M_6_3(alarm_sub_clock_1_out_a_m_6_3), .Out_A_M_9_1(alarm_sub_clock_1_out_a_m_9_1),
    .Out_A_M_9_2(alarm_sub_clock_1_out_a_m_9_2), .Out_A_M_9_3(alarm_sub_clock_1_out_a_m_9_3),
    .Out_A_M_9_4(alarm_sub_clock_1_out_a_m_9_4), .Clock(minutes_and_hours_1_out_clock), .Set_Time(or_1_out),
    .M_plus(M_plus), .H_plus(H_plus), .Enable_Alarm_LED(Enable_Alarm_LED));
  Enable_Alarm enable_alarm_1 (
    .Out_Alarm_LED(enable_alarm_1_out_alarm_led), .Out_H_6(enable_alarm_1_out_h_6),
    .Out_M_6_1(enable_alarm_1_out_m_6_1[0]), .Out_M_6_2(enable_alarm_1_out_m_6_1[1]),
    .Out_M_6_3(enable_alarm_1_out_m_6_1[2]), .Out_M_9_1(enable_alarm_1_out_m_9_1[0]),
    .Out_M_9_2(enable_alarm_1_out_m_9_1[1]), .Out_M_9_3(enable_alarm_1_out_m_9_1[2]),
    .Out_M_9_4(enable_alarm_1_out_m_9_1[3]), .Out_H_1(enable_alarm_1_out_h_1[0]),
    .Out_H_2(enable_alarm_1_out_h_1[1]), .Out_H_3(enable_alarm_1_out_h_1[2]),
    .Out_H_4(enable_alarm_1_out_h_1[3]), .Out_H_5(enable_alarm_1_out_h_5[0]), .En_Alarm(not_1_out),
    .Int_H_6(minutes_and_hours_1_out_h_6), .Int_A_M_6_1(alarm_sub_clock_1_out_a_m_6_1),
    .Int_A_M_6_2(alarm_sub_clock_1_out_a_m_6_2), .Int_A_M_6_3(alarm_sub_clock_1_out_a_m_6_3),
    .Int_A_M_9_1(alarm_sub_clock_1_out_a_m_9_1), .Int_A_M_9_2(alarm_sub_clock_1_out_a_m_9_2),
    .Int_A_M_9_3(alarm_sub_clock_1_out_a_m_9_3), .Int_A_M_9_4(alarm_sub_clock_1_out_a_m_9_4),
    .Int_A_H_1(alarm_sub_clock_1_out_a_h_1), .Int_M_6_1(minutes_and_hours_1_out_m_6_1),
    .Int_A_H_2(alarm_sub_clock_1_out_a_h_2), .Int_A_H_3(alarm_sub_clock_1_out_a_h_3),
    .Int_A_H_4(alarm_sub_clock_1_out_a_h_4), .Int_A_H_5(alarm_sub_clock_1_out_a_h_5),
    .Int_A_H_6(alarm_sub_clock_1_out_a_h_6), .Int_M_6_2(minutes_and_hours_1_out_m_6_2),
    .Int_M_6_3(minutes_and_hours_1_out_m_6_3), .Int_M_9_1(minutes_and_hours_1_out_m_9_1),
    .Int_M_9_2(minutes_and_hours_1_out_m_9_2), .Int_M_9_3(minutes_and_hours_1_out_m_9_3),
    .Int_M_9_4(minutes_and_hours_1_out_m_9_4), .Int_H_1(minutes_and_hours_1_out_h_1),
    .Int_H_2(minutes_and_hours_1_out_h_2), .Int_H_3(minutes_and_hours_1_out_h_3),
    .Int_H_4(minutes_and_hours_1_out_h_4), .Int_H_5(minutes_and_hours_1_out_h_5),
    .En_Alarm_LED(Enable_Alarm_LED));
  Hex_Digit_Display hex_digit_display_1 (.value({3'b000, enable_alarm_1_out_h_5[0]}));  // open: dp
  Hex_Digit_Display hex_digit_display_2 (.value(enable_alarm_1_out_h_1));  // open: dp
  Hex_Digit_Display hex_digit_display_3 (.value({1'b0, enable_alarm_1_out_m_6_1}));  // open: dp
  LED led_1 (.in(enable_alarm_1_out_alarm_led));
  Hex_Digit_Display hex_digit_display_4 (.value(enable_alarm_1_out_m_9_1));  // open: dp
  LED led_2 (.in(enable_alarm_1_out_h_6));

  // Notes on the sheet:
  //   Start
  //   Hours
  //   Minutes
  //   :
  //   Alarm LED
  //   AM/PM
endmodule

module Mod_six_counter (
  input  Clock_input,
  output Plus,
  output Bit1,
  output Bit2,
  output Bit3
);

  wire and_1_out;
  wire [3:3] not_1_out;

  J_K_Flip_Flop j_k_ff_1 (.J(1'b1), .K(1'b1), .clk(Clock_input), .Q(Bit1), .reset(Plus));  // open: Qn, preset
  J_K_Flip_Flop j_k_ff_2 (.J(Bit1), .K(Bit1), .clk(Clock_input), .Q(Bit2), .reset(Plus));  // open: Qn, preset
  and and_1 (and_1_out, Bit1, Bit2);
  J_K_Flip_Flop j_k_ff_3 (.J(and_1_out), .K(and_1_out), .clk(Clock_input), .Q(Bit3), .reset(Plus));  // open: Qn, preset
  and and_2 (Plus, Bit3, Bit2);
  not not_1 (not_1_out[3], 1'b1);
  Hex_Digit_Display hex_digit_display_1 (.value({not_1_out[3], Bit3, Bit2, Bit1}));  // open: dp
endmodule

module Mod_nine_counter (
  input  Clock_input,
  output Bit1,
  output Bit2,
  output Bit3,
  output Bit4,
  output Plus
);

  wire and_1_out, and_2_out, xor_1_out, xor_2_out;

  J_K_Flip_Flop #(.trigger("falling")) j_k_ff_1 (
    .J(1'b1), .K(1'b1), .clk(Clock_input), .Q(Bit1), .reset(Plus));  // open: Qn, preset
  J_K_Flip_Flop #(.trigger("falling")) j_k_ff_2 (
    .J(1'b1), .K(1'b1), .clk(Bit1), .Q(Bit2), .reset(Plus));  // open: Qn, preset
  xor xor_1 (xor_1_out, Bit1, Bit2);
  J_K_Flip_Flop #(.trigger("falling")) j_k_ff_3 (
    .J(1'b1), .K(1'b1), .clk(Bit2), .Q(Bit3), .reset(Plus));  // open: Qn, preset
  and and_1 (and_1_out, xor_1_out, xor_2_out);
  and and_2 (and_2_out, Bit2, Bit4);
  and and_3 (Plus, and_1_out, and_2_out);
  J_K_Flip_Flop #(.trigger("falling")) j_k_ff_4 (
    .J(1'b1), .K(1'b1), .clk(Bit3), .Q(Bit4), .reset(Plus));  // open: Qn, preset
  xor xor_2 (xor_2_out, Bit3, Bit4);
  Hex_Digit_Display hex_digit_display_1 (.value({Bit4, Bit3, Bit2, Bit1}));  // open: dp
endmodule

module Hours (
  input  Plus,
  output Bit01,
  output Bit02,
  output Bit03,
  output Bit04,
  output Bit05,
  output Bit06
);

  wire and_1_out, and_2_out, and_3_out, and_4_out, and_5_out, and_6_out, and_7_out, and_8_out, nor_1_out,
       not_1_out, not_3_out, or_1_out, or_2_out, or_3_out, or_4_out, xor_1_out, xor_2_out;
  wire [3:3] not_2_out;

  J_K_Flip_Flop #(.trigger("falling")) j_k_ff_1 (.J(1'b1), .K(1'b1), .clk(Plus), .Q(Bit01));  // open: Qn, preset, reset
  J_K_Flip_Flop #(.trigger("falling")) j_k_ff_2 (
    .J(1'b1), .K(1'b1), .clk(Bit01), .Q(Bit02), .reset(or_1_out));  // open: Qn, preset
  or or_1 (or_1_out, and_5_out, and_4_out);
  xor xor_1 (xor_1_out, Bit01, Bit02);
  J_K_Flip_Flop #(.trigger("falling")) j_k_ff_3 (
    .J(1'b1), .K(1'b1), .clk(Bit02), .Q(Bit03), .reset(or_2_out));  // open: Qn, preset
  or or_2 (or_2_out, and_5_out, and_4_out);
  and and_1 (and_1_out, Bit01, Bit02, not_1_out, Bit04);
  and and_2 (and_2_out, xor_1_out, xor_2_out);
  not not_1 (not_1_out, Bit03);
  and and_3 (and_3_out, Bit02, Bit04);
  and and_4 (and_4_out, and_2_out, and_3_out);
  J_K_Flip_Flop #(.trigger("falling")) j_k_ff_4 (
    .J(1'b1), .K(1'b1), .clk(Bit03), .Q(Bit04), .reset(or_3_out));  // open: Qn, preset
  or or_3 (or_3_out, and_5_out, and_4_out);
  xor xor_2 (xor_2_out, Bit03, Bit04);
  nor nor_1 (nor_1_out, Bit03, Bit04);
  J_K_Flip_Flop #(.trigger("falling")) j_k_ff_5 (
    .J(1'b1), .K(1'b1), .Q(Bit05), .preset(or_4_out), .reset(and_5_out));  // open: clk, Qn
  or or_4 (or_4_out, and_1_out, and_4_out);
  and and_5 (and_5_out, Bit05, and_6_out);
  and and_6 (and_6_out, Bit01, nor_1_out, Bit02);
  Hex_Digit_Display hex_digit_display_1 (.value({{3{not_2_out[3]}}, Bit05}));  // open: dp
  not not_2 (not_2_out[3], 1'b1);
  Hex_Digit_Display hex_digit_display_2 (.value({Bit04, Bit03, Bit02, Bit01}));  // open: dp
  and and_7 (and_7_out, and_5_out, not_3_out);
  J_K_Flip_Flop #(.trigger("falling")) j_k_ff_6 (
    .J(1'b1), .K(1'b1), .Q(Bit06), .preset(and_7_out), .reset(and_8_out));  // open: clk, Qn
  and and_8 (and_8_out, and_5_out, Bit06);
  not not_3 (not_3_out, Bit06);
endmodule

module Minutes (
  input  Start,
  output Plus,
  output Bit6_1,
  output Bit9_1,
  output Bit6_2,
  output Bit9_2,
  output Bit6_3,
  output Bit9_3,
  output Bit9_4
);

  wire mod_nine_counter_1_plus;
  wire [3:3] not_1_out;

  Mod_six_counter mod_six_counter_1 (
    .Clock_input(mod_nine_counter_1_plus), .Plus(Plus), .Bit1(Bit6_1), .Bit2(Bit6_2), .Bit3(Bit6_3));
  Hex_Digit_Display hex_digit_display_1 (.value({not_1_out[3], Bit6_3, Bit6_2, Bit6_1}));  // open: dp
  not not_1 (not_1_out[3], 1'b1);
  Hex_Digit_Display hex_digit_display_2 (.value({Bit9_4, Bit9_3, Bit9_2, Bit9_1}));  // open: dp
  Mod_nine_counter mod_nine_counter_1 (
    .Clock_input(Start), .Bit1(Bit9_1), .Bit2(Bit9_2), .Bit3(Bit9_3), .Bit4(Bit9_4),
    .Plus(mod_nine_counter_1_plus));
endmodule

module Minutes_and_Hours (
  input  Clock,
  input  Set_Time,
  input  M_plus,
  input  H_plus,
  output Out_Clock,
  output Out_M_6_1,
  output Out_H_1,
  output Out_M_6_2,
  output Out_H_2,
  output Out_M_6_3,
  output Out_H_3,
  output Out_M_9_1,
  output Out_H_4,
  output Out_M_9_2,
  output Out_H_5,
  output Out_M_9_3,
  output Out_H_6,
  output Out_M_9_4
);

  wire and_1_out, and_2_out, and_3_out, minutes_1_plus, not_1_out, or_1_out, or_2_out;

  or or_1 (or_1_out, minutes_1_plus, and_1_out);
  Hours hours_1 (
    .Plus(or_1_out), .Bit01(Out_H_1), .Bit02(Out_H_2), .Bit03(Out_H_3), .Bit04(Out_H_4), .Bit05(Out_H_5),
    .Bit06(Out_H_6));
  or or_2 (or_2_out, and_3_out, and_2_out);
  Hex_Digit_Display hex_digit_display_1 (.value({3'b000, Out_H_5}));  // open: dp
  Hex_Digit_Display hex_digit_display_2 (.value({Out_H_4, Out_H_3, Out_H_2, Out_H_1}));  // open: dp
  Minutes minutes_1 (
    .Start(or_2_out), .Plus(minutes_1_plus), .Bit6_1(Out_M_6_1), .Bit9_1(Out_M_9_1), .Bit6_2(Out_M_6_2),
    .Bit9_2(Out_M_9_2), .Bit6_3(Out_M_6_3), .Bit9_3(Out_M_9_3), .Bit9_4(Out_M_9_4));
  Hex_Digit_Display hex_digit_display_3 (.value({1'b0, Out_M_6_3, Out_M_6_2, Out_M_6_1}));  // open: dp
  and and_1 (and_1_out, Set_Time, H_plus);
  Hex_Digit_Display hex_digit_display_4 (.value({Out_M_9_4, Out_M_9_3, Out_M_9_2, Out_M_9_1}));  // open: dp
  and and_2 (and_2_out, Set_Time, M_plus);
  LED led_1 (.in(Out_H_6));
  and and_3 (and_3_out, Clock, not_1_out);
  not not_1 (not_1_out, Set_Time);

  assign Out_Clock = Clock;

  // Notes on the sheet:
  //   :
  //   AM/PM
endmodule

module Alarm_sub_Clock (
  input  Clock,
  input  Enable_Alarm_LED,
  input  Set_Time,
  input  M_plus,
  input  H_plus,
  output Out_A_M_6_1,
  output Out_A_H_1,
  output Out_A_M_6_2,
  output Out_A_H_2,
  output Out_A_M_6_3,
  output Out_A_H_3,
  output Out_A_M_9_1,
  output Out_A_H_4,
  output Out_A_M_9_2,
  output Out_A_H_5,
  output Out_A_M_9_3,
  output Out_A_H_6,
  output Out_A_M_9_4
);

  wire and_1_out, and_2_out, and_3_out, minutes_1_plus, not_1_out, not_2_out, or_1_out, or_2_out;

  or or_1 (or_1_out, minutes_1_plus, and_1_out);
  Hours hours_1 (
    .Plus(or_1_out), .Bit01(Out_A_H_1), .Bit02(Out_A_H_2), .Bit03(Out_A_H_3), .Bit04(Out_A_H_4),
    .Bit05(Out_A_H_5), .Bit06(Out_A_H_6));
  or or_2 (or_2_out, and_3_out, and_2_out);
  Hex_Digit_Display hex_digit_display_1 (.value({3'b000, Out_A_H_5}));  // open: dp
  Hex_Digit_Display hex_digit_display_2 (.value({Out_A_H_4, Out_A_H_3, Out_A_H_2, Out_A_H_1}));  // open: dp
  Minutes minutes_1 (
    .Start(or_2_out), .Plus(minutes_1_plus), .Bit6_1(Out_A_M_6_1), .Bit9_1(Out_A_M_9_1),
    .Bit6_2(Out_A_M_6_2), .Bit9_2(Out_A_M_9_2), .Bit6_3(Out_A_M_6_3), .Bit9_3(Out_A_M_9_3),
    .Bit9_4(Out_A_M_9_4));
  Hex_Digit_Display hex_digit_display_3 (.value({1'b0, Out_A_M_6_3, Out_A_M_6_2, Out_A_M_6_1}));  // open: dp
  and and_1 (and_1_out, Set_Time, H_plus);
  Hex_Digit_Display hex_digit_display_4 (.value({Out_A_M_9_4, Out_A_M_9_3, Out_A_M_9_2, Out_A_M_9_1}));  // open: dp
  and and_2 (and_2_out, Set_Time, M_plus);
  LED led_1 (.in(Out_A_H_6));
  and and_3 (and_3_out, Clock, not_1_out, not_2_out);
  not not_1 (not_1_out, Enable_Alarm_LED);
  not not_2 (not_2_out, Set_Time);

  // Notes on the sheet:
  //   :
  //   AM/PM
endmodule

module Enable_Alarm (
  input  En_Alarm,
  input  Int_M_6_1,
  input  Int_M_6_2,
  input  Int_M_6_3,
  input  Int_M_9_1,
  input  Int_M_9_2,
  input  Int_M_9_3,
  input  Int_M_9_4,
  input  Int_H_1,
  input  Int_H_2,
  input  Int_H_3,
  input  Int_H_4,
  input  Int_H_5,
  input  Int_H_6,
  input  Int_A_M_6_1,
  input  Int_A_M_6_2,
  input  Int_A_M_6_3,
  input  Int_A_M_9_1,
  input  Int_A_M_9_2,
  input  Int_A_M_9_3,
  input  Int_A_M_9_4,
  input  Int_A_H_1,
  input  Int_A_H_2,
  input  Int_A_H_3,
  input  Int_A_H_4,
  input  Int_A_H_5,
  input  Int_A_H_6,
  input  En_Alarm_LED,
  output Out_M_6_1,
  output Out_M_6_2,
  output Out_M_6_3,
  output Out_M_9_1,
  output Out_M_9_2,
  output Out_M_9_3,
  output Out_M_9_4,
  output Out_H_1,
  output Out_H_2,
  output Out_H_3,
  output Out_H_4,
  output Out_H_5,
  output Out_H_6,
  output Out_Alarm_LED
);

  wire and_1_out, and_2_out, and_4_out, and_5_out, and_6_out, and_7_out, and_8_out, and_9_out, and_10_out,
       and_11_out, and_12_out, and_13_out, and_14_out, and_15_out, and_16_out, and_17_out, and_18_out,
       and_19_out, and_20_out, and_21_out, and_22_out, and_23_out, and_24_out, and_25_out, and_26_out,
       and_27_out, and_28_out, and_29_out, not_1_out, not_2_out, not_3_out, not_4_out, not_5_out, not_6_out,
       not_7_out, not_8_out, not_9_out, not_10_out, not_11_out, not_12_out, not_13_out, not_14_out,
       not_15_out, t_ff_1_q, xor_1_out, xor_2_out, xor_3_out, xor_4_out, xor_5_out, xor_6_out, xor_7_out,
       xor_8_out, xor_9_out, xor_10_out, xor_11_out, xor_12_out, xor_13_out;

  xor xor_1 (xor_1_out, Int_M_6_1, Int_A_M_6_1);
  not not_1 (not_1_out, xor_1_out);
  xor xor_2 (xor_2_out, Int_M_6_2, Int_A_M_6_2);
  not not_2 (not_2_out, xor_2_out);
  xor xor_3 (xor_3_out, Int_M_6_3, Int_A_M_6_3);
  not not_3 (not_3_out, xor_3_out);
  xor xor_4 (xor_4_out, Int_M_9_1, Int_A_M_9_1);
  not not_4 (not_4_out, xor_4_out);
  xor xor_5 (xor_5_out, Int_M_9_2, Int_A_M_9_2);
  not not_5 (not_5_out, xor_5_out);
  xor xor_6 (xor_6_out, Int_M_9_3, Int_A_M_9_3);
  not not_6 (not_6_out, xor_6_out);
  xor xor_7 (xor_7_out, Int_M_9_4, Int_A_M_9_4);
  not not_7 (not_7_out, xor_7_out);
  and and_1 (and_1_out, not_1_out, not_2_out, not_3_out, not_4_out, not_5_out, not_6_out, not_7_out, not_8_out, not_9_out, not_10_out, not_11_out, not_12_out, not_14_out);
  xor xor_8 (xor_8_out, Int_H_1, Int_A_H_1);
  not not_8 (not_8_out, xor_8_out);
  xor xor_9 (xor_9_out, Int_H_2, Int_A_H_2);
  not not_9 (not_9_out, xor_9_out);
  xor xor_10 (xor_10_out, Int_H_3, Int_A_H_3);
  not not_10 (not_10_out, xor_10_out);
  xor xor_11 (xor_11_out, Int_H_4, Int_A_H_4);
  not not_11 (not_11_out, xor_11_out);
  and and_2 (and_2_out, En_Alarm_LED, and_1_out);
  T_Flip_Flop t_ff_1 (.T(1'b1), .clk(and_1_out), .Q(t_ff_1_q), .reset(not_13_out), .preset(and_2_out));  // open: Qn
  xor xor_12 (xor_12_out, Int_H_5, Int_A_H_5);
  not not_12 (not_12_out, xor_12_out);
  not not_13 (not_13_out, En_Alarm_LED);
  xor xor_13 (xor_13_out, Int_H_6, Int_A_H_6);
  not not_14 (not_14_out, xor_13_out);
  and and_3 (Out_Alarm_LED, t_ff_1_q, En_Alarm_LED);
  not not_15 (not_15_out, En_Alarm);
  LED led_1 (.in(Out_Alarm_LED));
  and and_4 (and_4_out, En_Alarm, Int_M_6_1);
  and and_5 (and_5_out, En_Alarm, Int_M_6_2);
  and and_6 (and_6_out, En_Alarm, Int_M_6_3);
  and and_7 (and_7_out, En_Alarm, Int_M_9_1);
  and and_8 (and_8_out, En_Alarm, Int_M_9_2);
  and and_9 (and_9_out, En_Alarm, Int_M_9_3);
  and and_10 (and_10_out, En_Alarm, Int_M_9_4);
  and and_11 (and_11_out, En_Alarm, Int_H_1);
  and and_12 (and_12_out, En_Alarm, Int_H_2);
  and and_13 (and_13_out, En_Alarm, Int_H_3);
  and and_14 (and_14_out, En_Alarm, Int_H_4);
  and and_15 (and_15_out, En_Alarm, Int_H_5);
  and and_16 (and_16_out, En_Alarm, Int_H_6);
  and and_17 (and_17_out, not_15_out, Int_A_M_6_1);
  and and_18 (and_18_out, not_15_out, Int_A_M_6_2);
  and and_19 (and_19_out, not_15_out, Int_A_M_6_3);
  and and_20 (and_20_out, not_15_out, Int_A_M_9_1);
  and and_21 (and_21_out, not_15_out, Int_A_M_9_2);
  and and_22 (and_22_out, not_15_out, Int_A_M_9_3);
  and and_23 (and_23_out, not_15_out, Int_A_M_9_4);
  and and_24 (and_24_out, not_15_out, Int_A_H_1);
  and and_25 (and_25_out, not_15_out, Int_A_H_2);
  and and_26 (and_26_out, not_15_out, Int_A_H_3);
  and and_27 (and_27_out, not_15_out, Int_A_H_4);
  and and_28 (and_28_out, not_15_out, Int_A_H_5);
  and and_29 (and_29_out, not_15_out, Int_A_H_6);
  or or_1 (Out_M_6_1, and_4_out, and_17_out);
  or or_2 (Out_M_6_2, and_5_out, and_18_out);
  or or_3 (Out_M_6_3, and_6_out, and_19_out);
  or or_4 (Out_M_9_1, and_7_out, and_20_out);
  or or_5 (Out_M_9_2, and_8_out, and_21_out);
  or or_6 (Out_M_9_3, and_9_out, and_22_out);
  or or_7 (Out_M_9_4, and_10_out, and_23_out);
  or or_8 (Out_H_1, and_11_out, and_24_out);
  or or_9 (Out_H_2, and_12_out, and_25_out);
  or or_10 (Out_H_3, and_13_out, and_26_out);
  or or_11 (Out_H_4, and_14_out, and_27_out);
  or or_12 (Out_H_5, and_15_out, and_28_out);
  or or_13 (Out_H_6, and_16_out, and_29_out);
endmodule
