// Logisim project HalfAdder.circ as structural Verilog: 1 circuit, main circuit main
module main (
  input  Input_1,
  input  Input_2
);

  wire and_1_out, xor_1_out;

  xor xor_1 (xor_1_out, Input_1, Input_2);
  and and_1 (and_1_out, Input_1, Input_2);
  LED led_1 (.in(xor_1_out));
  LED led_2 (.in(and_1_out));

  // Notes on the sheet:
  //   Sum Output
  //   Carry Output
endmodule
