// Logisim project Stack_with_parallel_D_Flip_flops.circ as structural Verilog: 1 circuit, main circuit main
module main (
  input  L_R,
  input  in_2,
  input  in_3,
  input  in_4,
  input  in_5
);

  wire and_1_out, and_2_out, and_3_out, and_4_out, and_5_out, and_6_out, and_7_out, and_8_out, and_9_out,
       clock_1_out, d_ff_1_q, d_ff_2_q, d_ff_3_q, d_ff_4_q, d_ff_5_q, d_ff_6_q, d_ff_7_q, d_ff_8_q,
       not_1_out, or_1_out, or_2_out, or_3_out, or_4_out;

  not not_1 (not_1_out, L_R);
  Clock clock_1 (.out(clock_1_out));
  and and_1 (and_1_out, L_R, in_3);
  and and_2 (and_2_out, not_1_out, d_ff_3_q);
  or or_1 (or_1_out, and_1_out, and_2_out);
  D_Flip_Flop d_ff_1 (.D(or_1_out), .clk(clock_1_out), .Q(d_ff_1_q), .reset(in_4));  // open: Qn, preset
  and and_3 (and_3_out, clock_1_out, in_5);
  LED led_1 (.in(d_ff_1_q));
  D_Flip_Flop d_ff_2 (.D(d_ff_1_q), .clk(and_3_out), .Q(d_ff_2_q));  // open: Qn, preset, reset
  and and_4 (and_4_out, L_R, d_ff_1_q);
  or or_2 (or_2_out, and_4_out, and_5_out);
  D_Flip_Flop d_ff_3 (.D(or_2_out), .clk(clock_1_out), .Q(d_ff_3_q), .reset(in_4));  // open: Qn, preset
  LED led_2 (.in(d_ff_2_q));
  and and_5 (and_5_out, not_1_out, d_ff_5_q);
  LED led_3 (.in(d_ff_3_q));
  and and_6 (and_6_out, L_R, d_ff_3_q);
  or or_3 (or_3_out, and_6_out, and_7_out);
  D_Flip_Flop d_ff_4 (.D(d_ff_3_q), .clk(and_3_out), .Q(d_ff_4_q));  // open: Qn, preset, reset
  LED led_4 (.in(d_ff_4_q));
  and and_7 (and_7_out, not_1_out, d_ff_7_q);
  D_Flip_Flop d_ff_5 (.D(or_3_out), .clk(clock_1_out), .Q(d_ff_5_q), .reset(in_4));  // open: Qn, preset
  LED led_5 (.in(d_ff_5_q));
  and and_8 (and_8_out, L_R, d_ff_5_q);
  D_Flip_Flop d_ff_6 (.D(d_ff_5_q), .clk(and_3_out), .Q(d_ff_6_q));  // open: Qn, preset, reset
  and and_9 (and_9_out, not_1_out, in_2);
  or or_4 (or_4_out, and_8_out, and_9_out);
  D_Flip_Flop d_ff_7 (.D(or_4_out), .clk(clock_1_out), .Q(d_ff_7_q), .reset(in_4));  // open: Qn, preset
  LED led_6 (.in(d_ff_6_q));
  LED led_7 (.in(d_ff_7_q));
  D_Flip_Flop d_ff_8 (.D(d_ff_7_q), .clk(and_3_out), .Q(d_ff_8_q));  // open: Qn, preset, reset
  LED led_8 (.in(d_ff_8_q));
endmodule
