// Logisim project lab01.circ as structural Verilog: 1 circuit, main circuit main
module main (
  input  in_1,
  input  in_2,
  input  in_3,
  input  in_4,
  input  in_5,
  input  in_6,
  input  in_7,
  input  in_8,
  input  in_9
);

  wire and_1_out, not_1_out, or_1_out, xnor_1_out, xor_1_out;

  or or_1 (or_1_out, in_1, in_2);
  and and_1 (and_1_out, in_3, in_4);
  not not_1 (not_1_out, in_5);
  xor xor_1 (xor_1_out, in_6, in_7);
  xnor xnor_1 (xnor_1_out, in_8, in_9);
  LED led_1 (.in(or_1_out));
  LED led_2 (.in(and_1_out));
  LED led_3 (.in(not_1_out));
  LED led_4 (.in(xor_1_out));
  LED led_5 (.in(xnor_1_out));
endmodule
